# Fritzing sketch sketch (saved by Fritzing 0.9.3b)

parts:
  microSD1 = MicroSD Card Module
  Heltec_WiFi_LoRa_32_V1 = Heltec WiFi LoRa 32 V2 [part_number=HTIT-WB32LA]

nets:
  N1: microSD1.GND, Heltec_WiFi_LoRa_32_V1.pin_18, Heltec_WiFi_LoRa_32_V1.pin_19
  N2: microSD1.VCC, Heltec_WiFi_LoRa_32_V1.pin_20
  N3: microSD1.MISO, Heltec_WiFi_LoRa_32_V1.pin_28
  N4: microSD1.MOSI, Heltec_WiFi_LoRa_32_V1.pin_5
  N5: microSD1.SCK, Heltec_WiFi_LoRa_32_V1.pin_31
  N6: microSD1.CS, Heltec_WiFi_LoRa_32_V1.pin_33

notes:
  Setei no código o gpio 2 como o pino CS do módulo SD, com o comando SD.begin(2);. Porém, mesmo assim o módulo ainda não funcionou junto do LoRa.

custom parts:
  Heltec WiFi LoRa 32 V2: Heltec WiFi LoRa 32 V2 WiFi LoRa 32 is a classic IoT dev-board designed & produced by Heltec Automation(TM). It’s a highly integrated product based on ESP32 + SX127x, it has Wi-Fi, BLE, LoRa functions, also Li-Po battery management system, 0.96″ OLED are also included. It’s the best choice for smart cities, smart farms, smart home, and IoT makers.
